# Fritzing sketch MikeFuckedUpFFS (saved by Fritzing 0.9.0b)

parts:
  IC2 = H-Bridge [package=THT]  # not connected
  R7 = Resistor [tolerance=±5% resistance=10k package=THT]
  R8 = Resistor [tolerance=±5% resistance=10k package=THT]
  R9 = Resistor [tolerance=±5% resistance=10k package=THT]
  R10 = Resistor [tolerance=±5% resistance=10k package=THT]
  R11 = Resistor [tolerance=±5% resistance=10k package=THT]
  R12 = Resistor [tolerance=±5% resistance=10k package=THT]
  Onderdeel1 = SRF05 Ultrasonic Rangefinder
  Onderdeel2 = SRF05 Ultrasonic Rangefinder
  BAT1 = BC9VPC [package=bc9vpc]  # not connected
  Onderdeel4 = SRF05 Ultrasonic Rangefinder
  Onderdeel5 = Arduino Uno (Rev3) - ICSP
  S1 = Pushbutton [package="[THT]"]

nets:
  N1: R7.Pin_0, Onderdeel5.D11_PWM/MOSI
  N2: R8.Pin_1, Onderdeel5.D6_PWM
  N3: R9.Pin_1, Onderdeel5.D4
  N4: R10.Pin_1, Onderdeel5.D5_PWM
  N5: R11.Pin_0, Onderdeel5.D10_PWM/SS
  N6: R12.Pin_0, Onderdeel5.D9_PWM
  VCC: Onderdeel1.VCC, Onderdeel4.VCC, Onderdeel5.5V
  N7: Onderdeel1.Trig, Onderdeel5.D8
  N8: Onderdeel1.Echo, Onderdeel5.A2
  GND: Onderdeel1.GND, Onderdeel2.GND, Onderdeel5.GND
  N9: Onderdeel2.Trig, Onderdeel5.A1
  N10: Onderdeel2.Echo, Onderdeel5.D3_PWM
  N11: Onderdeel4.Trig, Onderdeel5.D2
  N12: Onderdeel4.Echo, Onderdeel5.A0
  N13: Onderdeel5.D12/MISO, S1.Pin_2
  N14: Onderdeel5.D13/SCK, S1.Pin_4
