# Fritzing sketch schema motoren v1 (saved by Fritzing 0.9.2b)
breadboards: 1

parts:
  IC1 = H-Bridge [package=THT]
  M1 = DC Motor
  M2 = DC Motor
  Onderdeel1 = Arduino Uno (Rev3)
  R1 = Resistor [tolerance=±5% resistance=10k package=THT]
  R2 = Resistor [tolerance=±5% resistance=10k package=THT]

nets:
  N1: IC1.1_2EN, R1.Pin_1
  N2: IC1.1A, Onderdeel1.D3_PWM
  N3: IC1.1Y, M2.pin_2
  GND1: IC1.GND1, IC1.GND2, IC1.GND3, IC1.GND4, Onderdeel1.GND
  N4: IC1.2Y, M2.pin_1
  N5: IC1.2A, Onderdeel1.D4
  N6: IC1.VCC2, IC1.VCC1, Onderdeel1.5V
  N7: IC1.3_4EN, R2.Pin_1
  N8: IC1.3A, Onderdeel1.D6_PWM
  N9: IC1.3Y, M1.pin_2
  N10: IC1.4Y, M1.pin_1
  N11: IC1.4A, Onderdeel1.D7
  N12: Onderdeel1.D2, R1.Pin_0
  N13: Onderdeel1.D5_PWM, R2.Pin_0

notes:
  + -
  - +
