# Fritzing sketch schema motoren v3.1 (saved by Fritzing 0.9.2b)

parts:
  IC2 = H-Bridge [package=THT]  # not connected
  R7 = Resistor [tolerance=±5% resistance=10k package=THT]  # not connected
  R8 = Resistor [tolerance=±5% resistance=10k package=THT]  # not connected
  R9 = Resistor [tolerance=±5% resistance=10k package=THT]  # not connected
  R10 = Resistor [tolerance=±5% resistance=10k package=THT]  # not connected
  R11 = Resistor [tolerance=±5% resistance=10k package=THT]  # not connected
  R12 = Resistor [tolerance=±5% resistance=10k package=THT]  # not connected
  Onderdeel1 = SRF05 Ultrasonic Rangefinder
  Onderdeel2 = SRF05 Ultrasonic Rangefinder
  BAT1 = BC9VPC [package=bc9vpc]  # not connected
  Onderdeel4 = SRF05 Ultrasonic Rangefinder

nets:
  VCC: Onderdeel1.VCC, Onderdeel4.VCC
  GND: Onderdeel1.GND, Onderdeel2.GND, Onderdeel4.GND
