# Fritzing sketch schema sensoren v1 (saved by Fritzing 0.9.2b)
breadboards: 1

parts:
  Onderdeel1 = SRF05 Ultrasonic Rangefinder
  Onderdeel2 = SRF05 Ultrasonic Rangefinder
  Onderdeel3 = SRF05 Ultrasonic Rangefinder
  Onderdeel4 = Arduino Uno (Rev3)

nets:
  VCC: Onderdeel1.VCC, Onderdeel2.VCC, Onderdeel3.VCC, Onderdeel4.5V
  N1: Onderdeel1.Trig, Onderdeel4.D2
  N2: Onderdeel1.Echo, Onderdeel4.D5_PWM
  GND: Onderdeel1.GND, Onderdeel2.GND, Onderdeel3.GND, Onderdeel4.GND
  N3: Onderdeel2.Trig, Onderdeel4.D4
  N4: Onderdeel2.Echo, Onderdeel4.D7
  N5: Onderdeel3.Trig, Onderdeel4.D3_PWM
  N6: Onderdeel3.Echo, Onderdeel4.D6_PWM
